// Logisim project exam3.circ as structural Verilog: 5 circuits, main circuit sold
module move (
  input  [2:0] In,
  input  [2:0] Q,
  output [2:0] out_3
);

  wire and_1_out, and_2_out, and_3_out, and_4_out, and_5_out, and_6_out, and_7_out, and_8_out, and_9_out,
       and_10_out, and_11_out, not_1_out, not_2_out, not_3_out, not_4_out, not_5_out, not_6_out, not_7_out,
       not_8_out, not_9_out, not_10_out, not_11_out, not_12_out, not_13_out, not_14_out, not_15_out,
       not_16_out, not_17_out, not_18_out, not_19_out, not_20_out, not_21_out, not_22_out;

  not not_1 (not_1_out, In[0]);
  not not_2 (not_2_out, In[1]);
  not not_3 (not_3_out, In[2]);
  not not_4 (not_4_out, In[0]);
  not not_5 (not_5_out, In[2]);
  not not_6 (not_6_out, Q[1]);
  not not_7 (not_7_out, Q[0]);
  not not_8 (not_8_out, Q[2]);
  not not_9 (not_9_out, In[0]);
  not not_10 (not_10_out, In[1]);
  not not_11 (not_11_out, In[2]);
  not not_12 (not_12_out, Q[1]);
  not not_13 (not_13_out, Q[2]);
  not not_14 (not_14_out, Q[0]);
  not not_15 (not_15_out, Q[1]);
  not not_16 (not_16_out, In[0]);
  not not_17 (not_17_out, In[1]);
  not not_18 (not_18_out, In[2]);
  not not_19 (not_19_out, Q[0]);
  not not_20 (not_20_out, Q[1]);
  not not_21 (not_21_out, Q[2]);
  not not_22 (not_22_out, Q[0]);
  and and_1 (and_1_out, not_1_out, not_2_out, not_3_out, Q[0]);
  and and_2 (and_2_out, not_4_out, not_5_out, Q[0], not_6_out);
  and and_3 (and_3_out, In[0], not_7_out, not_8_out);
  and and_4 (and_4_out, not_9_out, not_10_out, not_11_out, Q[1]);
  and and_5 (and_5_out, In[1], not_12_out, not_13_out);
  and and_6 (and_6_out, In[0], not_14_out, Q[1]);
  and and_7 (and_7_out, In[0], Q[0], not_15_out);
  and and_8 (and_8_out, not_16_out, not_17_out, not_18_out, Q[2]);
  and and_9 (and_9_out, In[2], not_19_out, not_20_out, not_21_out);
  and and_10 (and_10_out, In[1], not_22_out, Q[1]);
  and and_11 (and_11_out, In[0], Q[0], Q[1]);
  or or_1 (out_3[0], and_1_out, and_2_out, and_3_out);
  or or_2 (out_3[1], and_4_out, and_5_out, and_6_out, and_7_out);
  or or_3 (out_3[2], and_8_out, and_9_out, and_10_out, and_11_out);
endmodule

module put (
  input  [2:0] I,
  input  [2:0] Q,
  output JGE,
  output [1:0] back
);

  wire and_1_out, and_2_out, and_3_out, and_4_out, and_5_out, and_6_out, and_7_out, and_8_out, and_9_out,
       and_10_out, and_11_out, not_1_out;

  and and_1 (and_1_out, Q[0], I[2]);
  and and_2 (and_2_out, Q[1], I[2]);
  and and_3 (and_3_out, Q[1], Q[0], I[1]);
  and and_4 (and_4_out, Q[2], I[0]);
  and and_5 (and_5_out, Q[2], I[1]);
  and and_6 (and_6_out, Q[2], I[2]);
  not not_1 (not_1_out, Q[0]);
  and and_7 (and_7_out, I[2], Q[2]);
  and and_8 (and_8_out, I[2], Q[0], Q[1]);
  or or_1 (JGE, and_1_out, and_2_out, and_3_out, and_4_out, and_5_out, and_6_out);
  and and_9 (and_9_out, I[2], Q[2]);
  or or_2 (back[0], and_9_out, and_10_out, and_11_out);
  and and_10 (and_10_out, I[2], not_1_out, Q[1]);
  and and_11 (and_11_out, I[1], Q[2]);
  or or_3 (back[1], and_7_out, and_8_out);
endmodule

module sold (
  input  [2:0] in_1,
  output out_2,
  output [1:0] out_3
);

  wire clock_1_out;
  wire [2:0] move_1_out_3, register_1_q;

  move move_1 (.In(in_1), .Q(register_1_q), .out_3(move_1_out_3));
  Register #(.width(3)) register_1 (.D(move_1_out_3), .Q(register_1_q), .clk(clock_1_out));  // open: en, clr
  Clock clock_1 (.out(clock_1_out));
  put put_1 (.I(in_1), .Q(register_1_q), .JGE(out_2), .back(out_3));
endmodule

module outmodle (
  input  i0,
  input  i1,
  input  i2,
  input  q0,
  input  q1,
  input  q2,
  output j,
  output r0,
  output r2
);

  wire and_1_out, and_2_out, and_3_out, and_4_out, and_5_out, and_6_out, and_7_out, and_8_out, and_9_out,
       and_10_out, and_11_out, not_1_out;

  and and_1 (and_1_out, q0, i2);
  and and_2 (and_2_out, q1, i2);
  and and_3 (and_3_out, q1, q0, i1);
  and and_4 (and_4_out, q2, i0);
  and and_5 (and_5_out, q2, i1);
  and and_6 (and_6_out, q2, i2);
  not not_1 (not_1_out, q0);
  and and_7 (and_7_out, i2, q2);
  and and_8 (and_8_out, i2, q0, q1);
  or or_1 (j, and_1_out, and_2_out, and_3_out, and_4_out, and_5_out, and_6_out);
  and and_9 (and_9_out, i2, q2);
  and and_10 (and_10_out, i2, not_1_out, q1);
  and and_11 (and_11_out, i1, q2);
  or or_2 (r2, and_7_out, and_8_out);
  or or_3 (r0, and_9_out, and_10_out, and_11_out);
endmodule

module movemodle (
  input  i0,
  input  i1,
  input  i2,
  input  q0,
  input  q1,
  input  q2,
  output r0,
  output r1,
  output r2
);

  wire and_1_out, and_2_out, and_3_out, and_4_out, and_5_out, and_6_out, and_7_out, and_8_out, and_9_out,
       and_10_out, and_11_out, not_1_out, not_2_out, not_3_out, not_4_out, not_5_out, not_6_out, not_7_out,
       not_8_out, not_9_out, not_10_out, not_11_out, not_12_out, not_13_out, not_14_out, not_15_out,
       not_16_out, not_17_out, not_18_out, not_19_out, not_20_out, not_21_out, not_22_out;

  not not_1 (not_1_out, i0);
  not not_2 (not_2_out, i1);
  not not_3 (not_3_out, i2);
  not not_4 (not_4_out, i0);
  not not_5 (not_5_out, i2);
  not not_6 (not_6_out, q1);
  not not_7 (not_7_out, q0);
  not not_8 (not_8_out, q2);
  not not_9 (not_9_out, i0);
  not not_10 (not_10_out, i1);
  not not_11 (not_11_out, i2);
  not not_12 (not_12_out, q1);
  not not_13 (not_13_out, q2);
  not not_14 (not_14_out, q0);
  not not_15 (not_15_out, q1);
  not not_16 (not_16_out, i0);
  not not_17 (not_17_out, i1);
  not not_18 (not_18_out, i2);
  not not_19 (not_19_out, q0);
  not not_20 (not_20_out, q1);
  not not_21 (not_21_out, q2);
  not not_22 (not_22_out, q0);
  and and_1 (and_1_out, not_1_out, not_2_out, not_3_out, q0);
  and and_2 (and_2_out, not_4_out, not_5_out, q0, not_6_out);
  and and_3 (and_3_out, i0, not_7_out, not_8_out);
  and and_4 (and_4_out, not_9_out, not_10_out, not_11_out, q1);
  and and_5 (and_5_out, i1, not_12_out, not_13_out);
  and and_6 (and_6_out, i0, not_14_out, q1);
  and and_7 (and_7_out, i0, q0, not_15_out);
  and and_8 (and_8_out, not_16_out, not_17_out, not_18_out, q2);
  and and_9 (and_9_out, i2, not_19_out, not_20_out, not_21_out);
  and and_10 (and_10_out, i1, not_22_out, q1);
  and and_11 (and_11_out, i0, q0, q1);
  or or_1 (r0, and_1_out, and_2_out, and_3_out);
  or or_2 (r1, and_4_out, and_5_out, and_6_out, and_7_out);
  or or_3 (r2, and_8_out, and_9_out, and_10_out, and_11_out);
endmodule
