// Logisim project sold.circ as structural Verilog: 4 circuits, main circuit exam3
module exam3 (
  input  [2:0] I1,
  output o0,
  output [1:0] out_3
);

  wire and_1_out, and_2_out, and_3_out, and_4_out, and_5_out, and_6_out, and_7_out, and_8_out, and_9_out,
       and_10_out, and_11_out, and_12_out, and_13_out, and_14_out, and_15_out, and_16_out, and_17_out,
       and_18_out, and_19_out, clock_1_out, not_1_out, not_2_out, not_3_out, not_4_out, not_5_out, not_6_out,
       not_7_out, not_8_out, not_9_out, not_10_out, not_11_out, not_12_out, not_13_out, not_14_out,
       not_15_out, not_16_out, not_17_out, not_18_out, or_1_out, or_2_out, or_3_out, or_4_out, or_5_out;
  wire [1:0] bit_extender_4_out, bit_extender_5_out, shifter_4_out;
  wire [2:0] adder_1_out, adder_2_out, bit_extender_1_out, bit_extender_2_out, bit_extender_3_out,
       register_1_q, shifter_1_out, shifter_2_out, shifter_3_out;

  not not_1 (not_1_out, I1[0]);
  not not_2 (not_2_out, I1[1]);
  not not_3 (not_3_out, I1[2]);
  not not_4 (not_4_out, I1[2]);
  not not_5 (not_5_out, I1[0]);
  not not_6 (not_6_out, I1[1]);
  not not_7 (not_7_out, I1[1]);
  not not_8 (not_8_out, register_1_q[0]);
  not not_9 (not_9_out, I1[2]);
  not not_10 (not_10_out, I1[0]);
  not not_11 (not_11_out, I1[2]);
  not not_12 (not_12_out, I1[1]);
  not not_13 (not_13_out, I1[2]);
  not not_14 (not_14_out, register_1_q[1]);
  not not_15 (not_15_out, register_1_q[2]);
  and and_1 (and_1_out, not_1_out, not_2_out, not_3_out, register_1_q[0]);
  and and_2 (and_2_out, I1[1], not_4_out, register_1_q[1]);
  and and_3 (and_3_out, I1[1], I1[2], register_1_q[2]);
  and and_4 (and_4_out, not_5_out, not_6_out, register_1_q[1]);
  and and_5 (and_5_out, not_7_out, I1[2], not_8_out);
  and and_6 (and_6_out, I1[1], not_9_out, register_1_q[2]);
  and and_7 (and_7_out, I1[1], I1[2], register_1_q[0]);
  and and_8 (and_8_out, I1[0], register_1_q[0]);
  and and_9 (and_9_out, not_10_out, not_11_out, register_1_q[2]);
  and and_10 (and_10_out, not_12_out, I1[2], register_1_q[1]);
  and and_11 (and_11_out, I1[1], not_13_out, not_14_out);
  and and_12 (and_12_out, I1[0], not_15_out);
  or or_1 (or_1_out, and_1_out, and_2_out, and_3_out);
  assign bit_extender_1_out = {{2{1'b0}}, or_1_out};  // Bit_Extender bit_extender_1
  assign bit_extender_2_out = {{2{1'b0}}, or_2_out};  // Bit_Extender bit_extender_2
  or or_2 (or_2_out, and_4_out, and_5_out, and_6_out, and_7_out, and_8_out);
  or or_3 (or_3_out, and_9_out, and_10_out, and_11_out, and_12_out);
  assign bit_extender_3_out = {{2{1'b0}}, or_3_out};  // Bit_Extender bit_extender_3
  Shifter #(.width(3)) shifter_1 (.in(bit_extender_1_out), .\dist (2'b10), .out(shifter_1_out));
  Shifter #(.width(3)) shifter_2 (.in(bit_extender_2_out), .\dist (2'b01), .out(shifter_2_out));
  Shifter #(.width(3)) shifter_3 (.in(bit_extender_3_out), .\dist (2'b00), .out(shifter_3_out));
  Adder #(.width(3)) adder_1 (.a(shifter_1_out), .b(shifter_2_out), .out(adder_1_out));  // open: cin, cout
  Adder #(.width(3)) adder_2 (.a(adder_1_out), .b(shifter_3_out), .out(adder_2_out));  // open: cin, cout
  Clock clock_1 (.out(clock_1_out));
  Register #(.width(3)) register_1 (.D(adder_2_out), .Q(register_1_q), .clk(clock_1_out));  // open: en, clr
  not not_16 (not_16_out, I1[2]);
  and and_13 (and_13_out, register_1_q[1], register_1_q[2], I1[0]);
  and and_14 (and_14_out, register_1_q[0], I1[0]);
  not not_17 (not_17_out, register_1_q[2]);
  not not_18 (not_18_out, I1[2]);
  and and_15 (and_15_out, register_1_q[2], I1[0]);
  and and_16 (and_16_out, register_1_q[1], I1[0]);
  and and_17 (and_17_out, register_1_q[1], register_1_q[2], not_16_out);
  or or_4 (or_4_out, and_13_out, and_14_out);
  and and_18 (and_18_out, register_1_q[1], not_17_out, I1[0]);
  or or_5 (or_5_out, and_18_out, and_19_out);
  and and_19 (and_19_out, register_1_q[0], not_18_out);
  or or_6 (o0, and_15_out, and_16_out, and_17_out, register_1_q[0]);
  assign bit_extender_4_out = {{1{1'b0}}, or_4_out};  // Bit_Extender bit_extender_4
  assign bit_extender_5_out = {{1{1'b0}}, or_5_out};  // Bit_Extender bit_extender_5
  Shifter #(.width(2)) shifter_4 (.in(bit_extender_4_out), .\dist (1'b1), .out(shifter_4_out));
  Adder #(.width(2)) adder_3 (.a(shifter_4_out), .b(bit_extender_5_out), .out(out_3));  // open: cin, cout
endmodule

module test (
  input  q0,
  input  q1,
  input  q2,
  input  S0,
  input  S1,
  input  S2,
  output o0,
  output o1,
  output o2
);

  wire and_1_out, and_2_out, and_3_out, and_4_out, and_5_out, and_6_out, and_7_out, and_8_out, and_9_out,
       and_10_out, and_11_out, and_12_out, not_1_out, not_2_out, not_3_out, not_4_out, not_5_out, not_6_out,
       not_7_out, not_8_out, not_9_out, not_10_out, not_11_out, not_12_out, not_13_out, not_14_out,
       not_15_out;

  not not_1 (not_1_out, q0);
  not not_2 (not_2_out, q2);
  not not_3 (not_3_out, S0);
  not not_4 (not_4_out, q0);
  not not_5 (not_5_out, S1);
  not not_6 (not_6_out, q1);
  not not_7 (not_7_out, q1);
  not not_8 (not_8_out, q2);
  not not_9 (not_9_out, q0);
  not not_10 (not_10_out, q1);
  not not_11 (not_11_out, S2);
  not not_12 (not_12_out, q0);
  not not_13 (not_13_out, q1);
  not not_14 (not_14_out, q2);
  not not_15 (not_15_out, q0);
  and and_1 (and_1_out, not_1_out, not_2_out, S0);
  and and_2 (and_2_out, q2, not_3_out);
  and and_3 (and_3_out, not_4_out, q1, not_5_out);
  and and_4 (and_4_out, q0, not_6_out, S1);
  and and_5 (and_5_out, not_7_out, not_8_out, S1);
  and and_6 (and_6_out, q2, S2);
  and and_7 (and_7_out, not_9_out, q1, S0);
  and and_8 (and_8_out, q0, not_10_out, not_11_out);
  and and_9 (and_9_out, q0, q1, S2);
  and and_10 (and_10_out, not_12_out, not_13_out, not_14_out, S2);
  and and_11 (and_11_out, not_15_out, q1, S1);
  and and_12 (and_12_out, q0, q1, S0);
  or or_1 (o0, and_1_out, and_2_out, and_3_out, and_4_out);
  or or_2 (o1, and_5_out, and_6_out, and_7_out, and_8_out, and_9_out);
  or or_3 (o2, and_10_out, and_11_out, and_12_out);
endmodule

module _2 (
  input  q0,
  input  q1,
  input  q2,
  input  S0,
  input  S1,
  input  S2,
  output o0,
  output o1,
  output o2
);

  wire and_1_out, and_2_out, and_3_out, and_4_out, and_5_out, and_6_out, and_7_out, not_1_out, not_2_out,
       not_3_out;

  not not_1 (not_1_out, S0);
  not not_2 (not_2_out, S0);
  not not_3 (not_3_out, q0);
  and and_1 (and_1_out, q2, S2);
  and and_2 (and_2_out, q0, q1, S2);
  and and_3 (and_3_out, q1, S2);
  and and_4 (and_4_out, q0, S2);
  and and_5 (and_5_out, q0, q1, not_1_out);
  and and_6 (and_6_out, q2, not_2_out);
  and and_7 (and_7_out, not_3_out, q1, S2);
  or or_1 (o2, and_1_out, and_2_out);
  or or_2 (o0, q2, and_3_out, and_4_out, and_5_out);
  or or_3 (o1, and_6_out, and_7_out);
endmodule

module mod5 (
  input  I0,
  input  I1,
  input  I2,
  input  I3,
  output O0,
  output O1,
  output O2
);

  wire and_1_out, and_2_out, and_3_out, and_4_out, and_5_out, and_6_out, and_7_out, and_8_out, and_9_out,
       and_10_out, and_11_out, and_12_out, not_1_out, not_2_out, not_3_out, not_4_out, not_5_out, not_6_out,
       not_7_out, not_8_out, not_9_out, not_10_out, not_11_out, not_12_out, not_13_out, not_14_out,
       not_15_out, not_16_out, not_17_out, not_18_out, not_19_out, not_20_out, not_21_out;

  not not_1 (not_1_out, I0);
  not not_2 (not_2_out, I1);
  not not_3 (not_3_out, I2);
  not not_4 (not_4_out, I0);
  not not_5 (not_5_out, I3);
  not not_6 (not_6_out, I2);
  not not_7 (not_7_out, I3);
  not not_8 (not_8_out, I1);
  not not_9 (not_9_out, I2);
  not not_10 (not_10_out, I0);
  and and_1 (and_1_out, not_10_out, not_11_out, I3);
  not not_11 (not_11_out, I1);
  not not_12 (not_12_out, I1);
  and and_2 (and_2_out, not_12_out, I2, I3);
  not not_13 (not_13_out, I2);
  and and_3 (and_3_out, I1, not_13_out, not_14_out);
  not not_14 (not_14_out, I3);
  and and_4 (and_4_out, I0, I1, not_15_out);
  not not_15 (not_15_out, I3);
  not not_16 (not_16_out, I0);
  not not_17 (not_17_out, I1);
  not not_18 (not_18_out, I3);
  not not_19 (not_19_out, I0);
  not not_20 (not_20_out, I1);
  not not_21 (not_21_out, I2);
  and and_5 (and_5_out, not_1_out, not_2_out, not_3_out, I3);
  and and_6 (and_6_out, not_4_out, I1, I2, not_5_out);
  and and_7 (and_7_out, I0, not_6_out, not_7_out);
  and and_8 (and_8_out, I0, not_8_out, I2, I3);
  and and_9 (and_9_out, I0, I1, not_9_out);
  or or_1 (O1, and_1_out, and_2_out, and_3_out, and_4_out);
  and and_10 (and_10_out, not_16_out, not_17_out, I2, not_18_out);
  and and_11 (and_11_out, not_19_out, I1, I2, I3);
  or or_2 (O2, and_10_out, and_11_out, and_12_out);
  and and_12 (and_12_out, I0, not_20_out, not_21_out, I3);
  or or_3 (O0, and_5_out, and_6_out, and_7_out, and_8_out, and_9_out);
endmodule
