// Logisim project test3.circ as structural Verilog: 1 circuit, main circuit xmod5
module xmod5 (
  input  in_1,
  output [2:0] out_2
);

  wire and_1_out, and_2_out, and_3_out, and_4_out, and_5_out, and_6_out, and_7_out, and_8_out, and_9_out,
       and_10_out, and_11_out, and_12_out, clock_1_out, not_1_out, not_2_out, not_3_out, not_4_out,
       not_5_out, not_6_out, not_7_out, not_8_out, not_9_out, not_10_out, not_11_out, not_12_out, not_13_out,
       not_14_out, not_15_out, not_16_out, not_17_out, not_18_out, not_19_out, not_20_out, not_21_out;
  wire [2:0] or_3_out;

  not not_1 (not_1_out, in_1);
  not not_2 (not_2_out, out_2[0]);
  not not_3 (not_3_out, out_2[1]);
  not not_4 (not_4_out, in_1);
  not not_5 (not_5_out, out_2[2]);
  not not_6 (not_6_out, out_2[1]);
  not not_7 (not_7_out, out_2[2]);
  not not_8 (not_8_out, out_2[0]);
  not not_9 (not_9_out, out_2[1]);
  not not_10 (not_10_out, in_1);
  and and_1 (and_1_out, not_10_out, not_11_out, out_2[2]);
  not not_11 (not_11_out, out_2[0]);
  not not_12 (not_12_out, out_2[0]);
  and and_2 (and_2_out, not_12_out, out_2[1], out_2[2]);
  not not_13 (not_13_out, out_2[1]);
  and and_3 (and_3_out, out_2[0], not_13_out, not_14_out);
  not not_14 (not_14_out, out_2[2]);
  and and_4 (and_4_out, in_1, out_2[0], not_15_out);
  not not_15 (not_15_out, out_2[2]);
  not not_16 (not_16_out, in_1);
  not not_17 (not_17_out, out_2[0]);
  not not_18 (not_18_out, out_2[2]);
  not not_19 (not_19_out, in_1);
  not not_20 (not_20_out, out_2[0]);
  not not_21 (not_21_out, out_2[1]);
  and and_5 (and_5_out, not_1_out, not_2_out, not_3_out, out_2[2]);
  and and_6 (and_6_out, not_4_out, out_2[0], out_2[1], not_5_out);
  and and_7 (and_7_out, in_1, not_6_out, not_7_out);
  and and_8 (and_8_out, in_1, not_8_out, out_2[1], out_2[2]);
  and and_9 (and_9_out, in_1, out_2[0], not_9_out);
  or or_1 (or_3_out[1], and_1_out, and_2_out, and_3_out, and_4_out);
  and and_10 (and_10_out, not_16_out, not_17_out, out_2[1], not_18_out);
  or or_2 (or_3_out[2], and_10_out, and_11_out, and_12_out);
  and and_11 (and_11_out, not_19_out, out_2[0], out_2[1], out_2[2]);
  and and_12 (and_12_out, in_1, not_20_out, not_21_out, out_2[2]);
  or or_3 (or_3_out[0], and_5_out, and_6_out, and_7_out, and_8_out, and_9_out);
  Clock clock_1 (.out(clock_1_out));
  Register #(.width(3)) register_1 (.D(or_3_out), .Q(out_2), .clk(clock_1_out));  // open: en, clr
endmodule
