// Logisim project test1.circ as structural Verilog: 1 circuit, main circuit test1
module test1 (
  input  [31:0] in_1,
  input  [31:0] in_2,
  input  [31:0] in_3,
  input  [31:0] in_4,
  output [31:0] out_5
);

  assign out_5 = in_1 & in_2 & in_3 & in_4;  // AND_Gate and_1, 32 bits wide
endmodule
